# Fritzing sketch cachalot_arduino (saved by Fritzing 0.9.4)
breadboards: 1

parts:
  Part1 = Arduino Nano (Rev3.0) (ICSP)
  U1 = Module 4 Relais 5V [package="Module 4 Relais 5V"]
  Mod1 = generic-ac-power-supply [package=THT]
  R1 = Resistor [tolerance=±5% resistance=10 package="0805 [SMD]"]
  100% = Round Pushbutton
  R3 = Resistor [tolerance=±5% resistance=10 package="0805 [SMD]"]
  R4 = Resistor [tolerance=±5% resistance=10 package="0805 [SMD]"]
  R5 = Resistor [tolerance=±5% resistance=10 package="0805 [SMD]"]
  80% = Round Pushbutton
  R6 = Resistor [tolerance=±5% resistance=10 package="0805 [SMD]"]
  60% = Round Pushbutton
  40% = Round Pushbutton
  20% = Round Pushbutton

nets:
  GND: Part1.GND, U1.GND, Mod1.pin3, 100%.leg0, 80%.leg0, 60%.leg0, 40%.leg0, 20%.leg0
  N1: Part1.D3, R6.Pin_0, 20%.leg1
  N2: Part1.D4, R4.Pin_0, 40%.leg1
  N3: Part1.D5, R5.Pin_0, 60%.leg1
  N4: Part1.D6, R3.Pin_0, 80%.leg1
  N5: Part1.D7, R1.Pin_0, 100%.leg1
  N6: Part1.D8, U1.IN1
  N7: Part1.D9, U1.IN2
  N8: Part1.VIN, Mod1.pin4
  5V: Part1.5V, U1.VCC, R1.Pin_1, R3.Pin_1, R4.Pin_1, R5.Pin_1, R6.Pin_1

custom parts:
  Module 4 Relais 5V: Module 4 Relais 5V 4x SPD-06VDC-SD-C
  generic-ac-power-supply: Generic ac power supply module. Use as is, or customize the svgs to fit your particular device (as they are all different.) Provides AC input and single DC output. This is variant 2, with pcb modified to match the url for a specific device.
